// Logisim project cpu (1).circ as structural Verilog: 19 circuits, main circuit main
module main (
  input  reset
);

  wire alu_1_lessthanoreq0, ALUsource, and_1_out, Branch, fallClk, inpt, jal, jr, JToPC, keyboard_1_avail,
       memory_latch_1_oe_latched, memory_latch_1_we_latched, MemRead, MemToReg, MemWrite, outpt, RegDst,
       RegWrite, RiseClk;
  wire [2:0] alucontrol_1_out_2, multiplexer_1_out, multiplexer_2_out;
  wire [3:0] rom_1_data;
  wire [7:0] keyboard;
  wire [11:0] Address, PC1;
  wire [15:0] addersixteen_2_result, alu_1_aluresult, memory_latch_1_address_latched,
       memory_latch_1_data_in_latched, multiplexer_3_out, multiplexer_4_out, multiplexer_5_out,
       multiplexer_6_out, multiplexer_7_out, multiplexer_8_out, multiplexer_9_out, PC_regout, ram_1_dout,
       registerfile_1_readdata2, rs, signextend_1_out_2;
  wire [15:12] JumpAddress;

  Clock clk (.out(RiseClk));
  Keyboard keyboard_1 (.clk(fallClk), .re(inpt), .clr(reset), .avail(keyboard_1_avail), .data(keyboard[6:0]));
  TTY #(.rows(13), .cols(80)) tty_1 (.data(rs[6:0]), .clk(RiseClk), .we(outpt), .clr(reset));
  not not_1 (fallClk, RiseClk);
  not not_2 (keyboard[7], keyboard_1_avail);
  ROM #(.addrWidth(16), .dataWidth(16)) rom_1 (.addr(PC_regout), .data({rom_1_data, Address}));
  singleRegister PC (.Reset(reset), .RegData(multiplexer_6_out), .WE(1'b1), .clk(fallClk), .RegOut(PC_regout));
  Multiplexer #(.width(3), .enable("false")) multiplexer_1 (
    .in0(Address[8:6]), .in1(Address[5:3]), .out(multiplexer_1_out), .sel(RegDst));
  controlSignals controlsignals_1 (
    .opcode(rom_1_data), .RegDst(RegDst), .RegWrite(RegWrite), .ALUsource(ALUsource), .MemWrite(MemWrite),
    .MemRead(MemRead), .MemToReg(MemToReg), .JToPC(JToPC), .Branch(Branch), .jal(jal), .jr(jr), .inpt(inpt),
    .outpt(outpt));
  addersixteen addersixteen_1 (.A(PC_regout), .B(16'h1), .result({JumpAddress, PC1}));  // open: C, Cout
  Multiplexer #(.width(3), .enable("false")) multiplexer_2 (
    .in0(multiplexer_1_out), .in1(3'b111), .out(multiplexer_2_out), .sel(jal));
  RegisterFile registerfile_1 (
    .Reset(reset), .ReadRegister1(Address[11:9]), .ReadRegister2(Address[8:6]),
    .WriteRegister(multiplexer_2_out), .WriteData(multiplexer_9_out), .RegWrite(RegWrite), .clk(RiseClk),
    .ReadData1(rs), .ReadData2(registerfile_1_readdata2));
  SignExtend signextend_1 (.Immediate(Address[5:0]), .out_2(signextend_1_out_2));
  Multiplexer #(.width(16), .enable("false")) multiplexer_3 (
    .in0(registerfile_1_readdata2), .in1(signextend_1_out_2), .out(multiplexer_3_out), .sel(ALUsource));
  ALUcontrol alucontrol_1 (.in_1(rom_1_data), .out_2(alucontrol_1_out_2));
  ALU alu_1 (
    .in1(rs), .in2(multiplexer_3_out), .ALUoperation(alucontrol_1_out_2),
    .LessThanOrEq0(alu_1_lessthanoreq0), .ALUresult(alu_1_aluresult));
  addersixteen addersixteen_2 (
    .A({JumpAddress, PC1}), .B(signextend_1_out_2), .result(addersixteen_2_result));  // open: C, Cout
  Multiplexer #(.width(16), .enable("false")) multiplexer_4 (
    .in0({JumpAddress, PC1}), .in1(addersixteen_2_result), .out(multiplexer_4_out), .sel(and_1_out));
  and and_1 (and_1_out, Branch, alu_1_lessthanoreq0);
  memory_latch memory_latch_1 (
    .address(alu_1_aluresult), .WE(MemWrite), .clk(fallClk), .data_in(registerfile_1_readdata2),
    .address_latched(memory_latch_1_address_latched), .WE_latched(memory_latch_1_we_latched),
    .OE_latched(memory_latch_1_oe_latched), .data_in_latched(memory_latch_1_data_in_latched));
  Multiplexer #(.width(16), .enable("false")) multiplexer_5 (
    .in0(multiplexer_4_out), .in1({JumpAddress, Address}), .out(multiplexer_5_out), .sel(JToPC));
  RAM #(.addrWidth(16), .dataWidth(16), .trigger("high"), .databus("bibus")) ram_1 (
    .addr(memory_latch_1_address_latched), .we(memory_latch_1_we_latched), .oe(memory_latch_1_oe_latched),
    .din(memory_latch_1_data_in_latched), .dout(ram_1_dout));
  Multiplexer #(.width(16), .enable("false")) multiplexer_6 (
    .in0(multiplexer_5_out), .in1(rs), .out(multiplexer_6_out), .sel(jr));
  Multiplexer #(.width(16), .enable("false")) multiplexer_7 (
    .in0(alu_1_aluresult), .in1(ram_1_dout), .out(multiplexer_7_out), .sel(MemToReg));
  Multiplexer #(.width(16), .enable("false")) multiplexer_8 (
    .in0(multiplexer_7_out), .in1({JumpAddress, PC1}), .out(multiplexer_8_out), .sel(jal));
  Multiplexer #(.width(16), .enable("false")) multiplexer_9 (
    .in0(multiplexer_8_out), .in1({{8{1'b0}}, keyboard}), .out(multiplexer_9_out), .sel(inpt));

  // Other names for the same wires on the sheet: JumpAddress[11:0] = Address; PC1[15:12] = JumpAddress

  // Notes on the sheet:
  //   contents of rom_1 (hex, n*v repeats v):
  //   2041 2082 20c3 2104 2145 2186 21c7 903f
endmodule

module memory_latch (
  input  [15:0] address,
  input  WE,
  input  clk,
  input  [15:0] data_in,
  output [15:0] address_latched,
  output WE_latched,
  output OE_latched,
  output [15:0] data_in_latched
);

  wire DMwe_latch_q;
  wire [15:0] addr_latch_q;

  Register #(.width(16), .trigger("falling")) addr_latch (
    .D(address), .en(WE), .clk(clk), .Q(addr_latch_q));  // open: clr
  D_Flip_Flop #(.trigger("falling")) DMwe_latch (.D(WE), .clk(clk), .Q(DMwe_latch_q));  // open: Qn, preset, reset
  Register #(.width(16), .trigger("falling")) data_to_be_written (
    .D(data_in), .en(WE), .clk(clk), .Q(data_in_latched));  // open: clr
  Multiplexer #(.width(16), .enable("false")) multiplexer_1 (
    .in0(address), .in1(addr_latch_q), .out(address_latched), .sel(DMwe_latch_q));
  and and_1 (WE_latched, clk, DMwe_latch_q);
  not not_1 (OE_latched, WE_latched);
endmodule

module RegisterFile (
  input  Reset,
  input  [2:0] ReadRegister1,
  input  [2:0] ReadRegister2,
  input  [2:0] WriteRegister,
  input  [15:0] WriteData,
  input  RegWrite,
  input  clk,
  output [15:0] ReadData1,
  output [15:0] ReadData2
);

  wire En0, En1, En2, En3, En4, En5, En6, En7, RegWrite0, RegWrite1, RegWrite2, RegWrite3, RegWrite4,
       RegWrite5, RegWrite6, RegWrite7, REn0, REn00, REn01, REn1, REn02, REn2, REn03, REn3, REn04, REn4,
       REn05, REn5, REn06, REn6, REn07, REn7;
  wire [15:0] Out1, Out2, Out3, Out4, Out5, Out6, Out7;

  // Probe on {16{1'b0}}
  singleRegister singleregister_1 (.Reset(Reset), .RegData(WriteData), .WE(RegWrite1), .clk(clk), .RegOut(Out1));
  singleRegister singleregister_2 (.Reset(Reset), .RegData(WriteData), .WE(RegWrite2), .clk(clk), .RegOut(Out2));
  singleRegister singleregister_3 (.Reset(Reset), .RegData(WriteData), .WE(RegWrite3), .clk(clk), .RegOut(Out3));
  // Probe on Out1
  // Probe on Out2
  // Probe on Out3
  // Probe on Out4
  singleRegister singleregister_4 (.Reset(Reset), .RegData(WriteData), .WE(RegWrite4), .clk(clk), .RegOut(Out4));
  // Probe on Out5
  singleRegister singleregister_5 (.Reset(Reset), .RegData(WriteData), .WE(RegWrite5), .clk(clk), .RegOut(Out5));
  // Probe on Out6
  singleRegister singleregister_6 (.Reset(Reset), .RegData(WriteData), .WE(RegWrite6), .clk(clk), .RegOut(Out6));
  // Probe on Out7
  singleRegister singleregister_7 (.Reset(Reset), .RegData(WriteData), .WE(RegWrite7), .clk(clk), .RegOut(Out7));
  assign ReadData1 = REn0 ? {16{1'b0}} : 16'bz;  // Controlled_Buffer controlled_buffer_1
  assign ReadData1 = REn1 ? Out1 : 16'bz;  // Controlled_Buffer controlled_buffer_2
  assign ReadData1 = REn2 ? Out2 : 16'bz;  // Controlled_Buffer controlled_buffer_3
  assign ReadData1 = REn3 ? Out3 : 16'bz;  // Controlled_Buffer controlled_buffer_4
  assign ReadData1 = REn4 ? Out4 : 16'bz;  // Controlled_Buffer controlled_buffer_5
  assign ReadData1 = REn5 ? Out5 : 16'bz;  // Controlled_Buffer controlled_buffer_6
  assign ReadData1 = REn6 ? Out6 : 16'bz;  // Controlled_Buffer controlled_buffer_7
  assign ReadData1 = REn7 ? Out7 : 16'bz;  // Controlled_Buffer controlled_buffer_8
  assign ReadData2 = REn00 ? {16{1'b0}} : 16'bz;  // Controlled_Buffer controlled_buffer_9
  assign ReadData2 = REn01 ? Out1 : 16'bz;  // Controlled_Buffer controlled_buffer_10
  assign ReadData2 = REn02 ? Out2 : 16'bz;  // Controlled_Buffer controlled_buffer_11
  assign ReadData2 = REn03 ? Out3 : 16'bz;  // Controlled_Buffer controlled_buffer_12
  assign ReadData2 = REn04 ? Out4 : 16'bz;  // Controlled_Buffer controlled_buffer_13
  assign ReadData2 = REn05 ? Out5 : 16'bz;  // Controlled_Buffer controlled_buffer_14
  assign ReadData2 = REn06 ? Out6 : 16'bz;  // Controlled_Buffer controlled_buffer_15
  assign ReadData2 = REn07 ? Out7 : 16'bz;  // Controlled_Buffer controlled_buffer_16
  Decoder #(.select(3)) decoder_1 (
    .out0(En0), .out1(En1), .out2(En2), .out3(En3), .out4(En4), .out5(En5), .out6(En6), .out7(En7),
    .sel(WriteRegister));  // open: en
  Decoder #(.select(3)) decoder_2 (
    .out0(REn0), .out1(REn1), .out2(REn2), .out3(REn3), .out4(REn4), .out5(REn5), .out6(REn6), .out7(REn7),
    .sel(ReadRegister1));  // open: en
  Decoder #(.select(3)) decoder_3 (
    .out0(REn00), .out1(REn01), .out2(REn02), .out3(REn03), .out4(REn04), .out5(REn05), .out6(REn06),
    .out7(REn07), .sel(ReadRegister2));  // open: en
  and and_1 (RegWrite0, En0, RegWrite);
  and and_2 (RegWrite1, En1, RegWrite);
  and and_3 (RegWrite2, En2, RegWrite);
  and and_4 (RegWrite3, En3, RegWrite);
  and and_5 (RegWrite4, En4, RegWrite);
  and and_6 (RegWrite5, En5, RegWrite);
  and and_7 (RegWrite6, En6, RegWrite);
  and and_8 (RegWrite7, En7, RegWrite);
endmodule

module SignExtend (
  input  [5:0] Immediate,
  output [15:0] out_2
);

  assign out_2 = {{10{Immediate[5]}}, Immediate};  // Bit_Extender bit_extender_1
endmodule

module singleRegister (
  input  Reset,
  input  [15:0] RegData,
  input  WE,
  input  clk,
  output [15:0] RegOut
);

  wire and_1_out, and_2_out, and_3_out, and_4_out, and_5_out, and_6_out, and_7_out, and_8_out, and_9_out,
       and_10_out, and_11_out, and_12_out, and_13_out, and_14_out, and_15_out, and_16_out;

  and and_1 (and_1_out, WE, clk);
  and and_2 (and_2_out, WE, clk);
  D_Flip_Flop d_ff_1 (.D(RegData[0]), .clk(and_1_out), .Q(RegOut[0]), .reset(Reset));  // open: Qn, preset
  D_Flip_Flop d_ff_2 (.D(RegData[1]), .clk(and_2_out), .Q(RegOut[1]), .reset(Reset));  // open: Qn, preset
  D_Flip_Flop d_ff_3 (.D(RegData[2]), .clk(and_3_out), .Q(RegOut[2]), .reset(Reset));  // open: Qn, preset
  and and_3 (and_3_out, WE, clk);
  and and_4 (and_4_out, WE, clk);
  and and_5 (and_5_out, WE, clk);
  and and_6 (and_6_out, WE, clk);
  and and_7 (and_7_out, WE, clk);
  and and_8 (and_8_out, WE, clk);
  and and_9 (and_9_out, WE, clk);
  and and_10 (and_10_out, WE, clk);
  and and_11 (and_11_out, WE, clk);
  D_Flip_Flop d_ff_4 (.D(RegData[3]), .clk(and_4_out), .Q(RegOut[3]), .reset(Reset));  // open: Qn, preset
  D_Flip_Flop d_ff_5 (.D(RegData[4]), .clk(and_5_out), .Q(RegOut[4]), .reset(Reset));  // open: Qn, preset
  D_Flip_Flop d_ff_6 (.D(RegData[5]), .clk(and_6_out), .Q(RegOut[5]), .reset(Reset));  // open: Qn, preset
  D_Flip_Flop d_ff_7 (.D(RegData[6]), .clk(and_7_out), .Q(RegOut[6]), .reset(Reset));  // open: Qn, preset
  D_Flip_Flop d_ff_8 (.D(RegData[7]), .clk(and_8_out), .Q(RegOut[7]), .reset(Reset));  // open: Qn, preset
  D_Flip_Flop d_ff_9 (.D(RegData[8]), .clk(and_9_out), .Q(RegOut[8]), .reset(Reset));  // open: Qn, preset
  D_Flip_Flop d_ff_10 (.D(RegData[9]), .clk(and_10_out), .Q(RegOut[9]), .reset(Reset));  // open: Qn, preset
  D_Flip_Flop d_ff_11 (.D(RegData[10]), .clk(and_11_out), .Q(RegOut[10]), .reset(Reset));  // open: Qn, preset
  D_Flip_Flop d_ff_12 (.D(RegData[11]), .clk(and_12_out), .Q(RegOut[11]), .reset(Reset));  // open: Qn, preset
  and and_12 (and_12_out, WE, clk);
  and and_13 (and_13_out, WE, clk);
  and and_14 (and_14_out, WE, clk);
  and and_15 (and_15_out, WE, clk);
  and and_16 (and_16_out, WE, clk);
  D_Flip_Flop d_ff_13 (.D(RegData[12]), .clk(and_13_out), .Q(RegOut[12]), .reset(Reset));  // open: Qn, preset
  D_Flip_Flop d_ff_14 (.D(RegData[13]), .clk(and_14_out), .Q(RegOut[13]), .reset(Reset));  // open: Qn, preset
  D_Flip_Flop d_ff_15 (.D(RegData[14]), .clk(and_15_out), .Q(RegOut[14]), .reset(Reset));  // open: Qn, preset
  D_Flip_Flop d_ff_16 (.D(RegData[15]), .clk(and_16_out), .Q(RegOut[15]), .reset(Reset));  // open: Qn, preset

  // Other names for the same wires on the sheet: in0 = RegData[0]; Regln[15:0] = RegData; in1 = RegData[1];
  //   in2 = RegData[2]; in3 = RegData[3]; in4 = RegData[4]; in5 = RegData[5]; in6 = RegData[6]; in7 = RegData[7];
  //   in8 = RegData[8]; in9 = RegData[9]; in10 = RegData[10]; in11 = RegData[11]; in12 = RegData[12];
  //   in13 = RegData[13]; in14 = RegData[14]; in15 = RegData[15]; Out0 = RegOut[0]; Out1 = RegOut[1];
  //   Out2 = RegOut[2]; Out3 = RegOut[3]; Out4 = RegOut[4]; Out5 = RegOut[5]; Out6 = RegOut[6]; Out7 = RegOut[7];
  //   Out8 = RegOut[8]; Out9 = RegOut[9]; Out10 = RegOut[10]; Out11 = RegOut[11]; Out12 = RegOut[12];
  //   Out13 = RegOut[13]; Out14 = RegOut[14]; Out15 = RegOut[15]
endmodule

module ALU (
  input  [15:0] in1,
  input  [15:0] in2,
  input  [2:0] ALUoperation,
  output LessThanOrEq0,
  output [15:0] ALUresult
);

  wire and_1_out, and_2_out, nor_1_out;
  wire [15:0] ADD_result, Addi, not_1_out, not_2_out, shiftleft_1_out_3, shiftright_1_out_3, Sub, xor_1_out;

  assign not_1_out = ~in2;  // NOT_Gate not_1, 16 bits wide
  assign not_2_out = ~in1;  // NOT_Gate not_2, 16 bits wide
  assign xor_1_out = in1 ^ in2;  // XOR_Gate xor_1, 16 bits wide
  addersixteen ADD (.A(in1), .B(in2), .result(ADD_result));  // open: C, Cout
  addersixteen u_SUB (.A(in1), .B(not_1_out), .C(1'b1), .result(Sub));  // open: Cout
  addersixteen u_ADDI (.A(in1), .B(in2), .result(Addi));  // open: C, Cout
  ShiftLeft shiftleft_1 (.in_1(in1), .ShiftAmt(in2[2:0]), .out_3(shiftleft_1_out_3));
  ShiftRight shiftright_1 (.in_1(in1), .in_2(in2[2:0]), .out_3(shiftright_1_out_3));
  Multiplexer #(.select(3), .width(16), .enable("false")) multiplexer_1 (
    .in0(ADD_result), .in1(Sub), .in2(Addi), .in3(not_2_out), .in4(xor_1_out), .in5(shiftleft_1_out_3),
    .in6(shiftright_1_out_3), .in7(Addi), .out(ALUresult), .sel(ALUoperation));
  nor nor_1 (nor_1_out, in1[0], in1[1], in1[2], in1[3], in1[4], in1[5], in1[6], in1[7], in1[8], in1[9], in1[10], in1[11], in1[12], in1[13], in1[14], in1[15]);
  and and_1 (and_1_out, nor_1_out, ALUoperation[0]);
  and and_2 (and_2_out, ALUoperation[1], Sub[15]);
  or or_1 (LessThanOrEq0, and_1_out, and_2_out);

  // Other names for the same wires on the sheet: ShiftAmt[2:0] = in2[2:0]
endmodule

module ALUcontrol (
  input  [3:0] in_1,
  output [2:0] out_2
);


  assign out_2 = in_1[2:0];
endmodule

module controlSignals (
  input  [3:0] opcode,
  output RegDst,
  output RegWrite,
  output ALUsource,
  output MemWrite,
  output MemRead,
  output MemToReg,
  output JToPC,
  output Branch,
  output jal,
  output jr,
  output inpt,
  output outpt
);

  wire add, addi, beqz, blt, j, notInst, sllOp, srlOp, sub, XorOp;

  Decoder #(.select(4), .enable("false")) decoder_1 (
    .out0(add), .out1(sub), .out2(addi), .out3(notInst), .out4(XorOp), .out5(sllOp), .out6(srlOp),
    .out7(MemRead), .out8(MemWrite), .out9(beqz), .out10(blt), .out11(j), .out12(jr), .out13(jal),
    .out14(inpt), .out15(outpt), .sel(opcode));
  or or_1 (RegDst, add, sub, notInst, XorOp, sllOp, srlOp, jr, inpt, outpt);
  or or_2 (RegWrite, RegDst, addi, MemRead, jal);
  or or_3 (ALUsource, addi, sllOp, MemRead, srlOp, MemWrite);
  or or_4 (JToPC, j, jal);
  or or_5 (Branch, beqz, blt);

  assign MemToReg = MemRead;

  // Other names for the same wires on the sheet: lw = MemRead; RFormat = RegDst; sw = MemWrite
endmodule

module oneBitAdder (
  input  A,
  input  B,
  input  C,
  output S,
  output Cout
);

  wire and_1_out, and_2_out, xor_1_out;

  xor xor_1 (xor_1_out, A, B);
  and and_1 (and_1_out, C, xor_1_out);
  and and_2 (and_2_out, B, A);
  xor xor_2 (S, xor_1_out, C);
  or or_1 (Cout, and_1_out, and_2_out);

  // Other names for the same wires on the sheet: inA = A; inB = B; inC = C
endmodule

module fourBitAdder (
  input  [3:0] A,
  input  [3:0] B,
  input  C,
  output [3:0] result,
  output Cout
);

  wire C1, C2, C3;

  oneBitAdder onebitadder_1 (.A(A[0]), .B(B[0]), .C(C), .S(result[0]), .Cout(C1));
  oneBitAdder onebitadder_2 (.A(A[1]), .B(B[1]), .C(C1), .S(result[1]), .Cout(C2));
  oneBitAdder onebitadder_3 (.A(A[2]), .B(B[2]), .C(C2), .S(result[2]), .Cout(C3));
  oneBitAdder onebitadder_4 (.A(A[3]), .B(B[3]), .C(C3), .S(result[3]), .Cout(Cout));
endmodule

module addersixteen (
  input  [15:0] A,
  input  [15:0] B,
  input  C,
  output [15:0] result,
  output Cout
);

  wire C0, C1, C2;

  fourBitAdder fourbitadder_1 (.A(A[3:0]), .B(B[3:0]), .C(C), .result(result[3:0]), .Cout(C0));
  fourBitAdder fourbitadder_2 (.A(A[7:4]), .B(B[7:4]), .C(C0), .result(result[7:4]), .Cout(C1));
  fourBitAdder fourbitadder_3 (.A(A[11:8]), .B(B[11:8]), .C(C1), .result(result[11:8]), .Cout(C2));
  fourBitAdder fourbitadder_4 (.A(A[15:12]), .B(B[15:12]), .C(C2), .result(result[15:12]), .Cout(Cout));
endmodule

module ShiftLeftOne (
  input  [15:0] in_1,
  output [15:0] out_2
);


  assign out_2 = {in_1[14:0], 1'b0};
endmodule

module ShiftLeftTwo (
  input  [15:0] in_1,
  output [15:0] out_2
);

  wire [15:0] shiftleftone_1_out_2;

  ShiftLeftOne shiftleftone_1 (.in_1(in_1), .out_2(shiftleftone_1_out_2));
  ShiftLeftOne shiftleftone_2 (.in_1(shiftleftone_1_out_2), .out_2(out_2));
endmodule

module ShiftLeftFour (
  input  [15:0] in_1,
  output [15:0] out_2
);

  wire [15:0] shiftlefttwo_1_out_2;

  ShiftLeftTwo shiftlefttwo_1 (.in_1(in_1), .out_2(shiftlefttwo_1_out_2));
  ShiftLeftTwo shiftlefttwo_2 (.in_1(shiftlefttwo_1_out_2), .out_2(out_2));
endmodule

module ShiftRightOne (
  input  [15:0] in_1,
  output [15:0] out_2
);


  assign out_2 = {1'b0, in_1[15:1]};
endmodule

module ShiftRightTwo (
  input  [15:0] in_1,
  output [15:0] out_2
);

  wire [15:0] shiftrightone_1_out_2;

  ShiftRightOne shiftrightone_1 (.in_1(in_1), .out_2(shiftrightone_1_out_2));
  ShiftRightOne shiftrightone_2 (.in_1(shiftrightone_1_out_2), .out_2(out_2));
endmodule

module ShiftRightFour (
  input  [15:0] in_1,
  output [15:0] out_2
);

  wire [15:0] shiftrighttwo_1_out_2;

  ShiftRightTwo shiftrighttwo_1 (.in_1(in_1), .out_2(shiftrighttwo_1_out_2));
  ShiftRightTwo shiftrighttwo_2 (.in_1(shiftrighttwo_1_out_2), .out_2(out_2));
endmodule

module ShiftLeft (
  input  [15:0] in_1,
  input  [2:0] ShiftAmt,
  output [15:0] out_3
);

  wire [15:0] multiplexer_1_out, multiplexer_2_out, shiftleftfour_1_out_2, shiftleftone_1_out_2,
       shiftlefttwo_1_out_2;

  ShiftLeftOne shiftleftone_1 (.in_1(in_1), .out_2(shiftleftone_1_out_2));
  Multiplexer #(.width(16), .enable("false")) multiplexer_1 (
    .in0(in_1), .in1(shiftleftone_1_out_2), .out(multiplexer_1_out), .sel(ShiftAmt[0]));
  ShiftLeftTwo shiftlefttwo_1 (.in_1(multiplexer_1_out), .out_2(shiftlefttwo_1_out_2));
  Multiplexer #(.width(16), .enable("false")) multiplexer_2 (
    .in0(multiplexer_1_out), .in1(shiftlefttwo_1_out_2), .out(multiplexer_2_out), .sel(ShiftAmt[1]));
  ShiftLeftFour shiftleftfour_1 (.in_1(multiplexer_2_out), .out_2(shiftleftfour_1_out_2));
  Multiplexer #(.width(16), .enable("false")) multiplexer_3 (
    .in0(multiplexer_2_out), .in1(shiftleftfour_1_out_2), .out(out_3), .sel(ShiftAmt[2]));

  // Other names for the same wires on the sheet: Bit0 = ShiftAmt[0]; Bit1 = ShiftAmt[1]; Bit2 = ShiftAmt[2]
endmodule

module ShiftRight (
  input  [15:0] in_1,
  input  [2:0] in_2,
  output [15:0] out_3
);

  wire [15:0] multiplexer_1_out, multiplexer_2_out, shiftrightfour_1_out_2, shiftrightone_1_out_2,
       shiftrighttwo_1_out_2;

  ShiftRightOne shiftrightone_1 (.in_1(in_1), .out_2(shiftrightone_1_out_2));
  Multiplexer #(.width(16), .enable("false")) multiplexer_1 (
    .in0(in_1), .in1(shiftrightone_1_out_2), .out(multiplexer_1_out), .sel(in_2[0]));
  ShiftRightTwo shiftrighttwo_1 (.in_1(multiplexer_1_out), .out_2(shiftrighttwo_1_out_2));
  Multiplexer #(.width(16), .enable("false")) multiplexer_2 (
    .in0(multiplexer_1_out), .in1(shiftrighttwo_1_out_2), .out(multiplexer_2_out), .sel(in_2[1]));
  ShiftRightFour shiftrightfour_1 (.in_1(multiplexer_2_out), .out_2(shiftrightfour_1_out_2));
  Multiplexer #(.width(16), .enable("false")) multiplexer_3 (
    .in0(multiplexer_2_out), .in1(shiftrightfour_1_out_2), .out(out_3), .sel(in_2[2]));

  // Other names for the same wires on the sheet: Bit0 = in_2[0]; Bit1 = in_2[1]; Bit2 = in_2[2]
endmodule
